# Fritzing sketch badwolf (saved by Fritzing 0.9.2b)
circuit board: 3.76906cm x 4.32439cm
breadboards: 1

parts:
  M1 = Stepper Motor - Unipolar
  IC1 = L293D [package=THT]
  Raspberry_Pi1 = Raspberry Pi B rev2

nets:
  N1: M1.C, IC1.Out_2_(_Controlled_by_Enable_1_)
  N2: M1.B, IC1.Out_3_(_Controlled_by_Enable_2_)
  N3: M1.COMMON_2, IC1.Out_1_(_Controlled_by_Enable_1_)
  N4: M1.D, IC1.Out_4_(_Controlled_by_Enable_2_)
  N5: IC1.Enable_1, IC1.Enable_2, Raspberry_Pi1.GPIO_18
  N6: IC1.In_1, Raspberry_Pi1.GPIO_4
  N7: IC1.0V, Raspberry_Pi1.GND
  N8: IC1.In_2, Raspberry_Pi1.GPIO_17
  N9: IC1.+Vmotor, IC1.+V, Raspberry_Pi1.5V
  N10: IC1.In_3, Raspberry_Pi1.GPIO_24
  N11: IC1.In_4, Raspberry_Pi1.GPIO_23

notes:
  ^
  .
  badwolf v3
